// Logisim project fic_processor.circ as structural Verilog: 2 circuits, main circuit main
module main (
  output halt,
  output [15:0] A_o,
  output [15:0] X_o,
  output [15:0] Y_o,
  output [15:0] PC,
  output [15:0] SP,
  output [3:0] FLAG
);

  wire aluOpSel, B_SUB, C_ADD, CLK, isCall, isRet;
  wire [1:0] FLAGIN;
  wire [3:0] ALUOP, cAluOp, SHAMT;
  wire [7:0] bit_extender_1_out, bit_extender_5_out;
  wire [9:0] ADDR10;
  wire [15:0] ADDREXT, ALURES, IMMEXT, MEMADDR, MEMDATA, MEMWDATA, NREGBIT, OPND, PCLOAD, PCPLUS1, PCTARGET,
       R_ADD, R_AND, R_DEC, R_DIV, R_INC, R_LSL, R_LSR, R_MOD, R_MUL, R_NOT, R_OR, R_RSL, R_RSR, R_SUB,
       R_XOR, REGWDATA, SPDECV, spEn, weX, weY;
  wire [15:4] undriven;
  wire [15:10] INSTR;
  wire [19:0] CW;

  Clock clock_1 (.out(CLK));
  Counter #(.width(16), .max('hffff)) u_PC (
    .load(PCLOAD[0]), .D(PCTARGET), .count(1'b1), .Q(PC), .up(1'b1), .clk(CLK), .clr(1'b0));  // open: carry
  Bit_Extender #(.in_width(16), .out_width(8), .\type ("zero")) bit_extender_1 (.in(PC), .out(bit_extender_1_out));
  ROM #(.addrWidth(8), .dataWidth(16)) PROG (.addr(bit_extender_1_out), .data({INSTR, ADDR10}));
  ROM #(.addrWidth(6), .dataWidth(20)) CTRL (.addr(INSTR), .data({CW[19], aluOpSel, cAluOp, halt, CW[12:0]}));
  assign IMMEXT = {{7{ADDR10[8]}}, ADDR10[8:0]};  // Bit_Extender bit_extender_2
  assign ADDREXT = {{6{1'b0}}, ADDR10};  // Bit_Extender bit_extender_3
  not not_1 (NREGBIT[0], ADDR10[9]);
  or or_1 (spEn[0], CW[11], CW[12]);
  Comparator #(.width(3)) comparator_1 (.a(CW[10:8]), .b(3'b110), .eq(isCall));  // open: gt, lt
  Adder #(.width(16)) adder_1 (.a(PC), .b(16'h1), .out(PCPLUS1), .cin(1'b0));  // open: cout
  Comparator #(.width(3)) comparator_2 (.a(CW[10:8]), .b(3'b111), .eq(isRet));  // open: gt, lt
  and and_1 (weX[0], CW[1], NREGBIT[0]);
  and and_2 (weY[0], CW[1], ADDR10[9]);
  Multiplexer #(.select(1), .width(4), .enable("false")) multiplexer_1 (
    .in0(INSTR[13:10]), .in1(cAluOp), .out(ALUOP), .sel(aluOpSel));
  Multiplexer #(.select(1), .width(16), .enable("false")) multiplexer_2 (
    .in0(X_o), .in1(Y_o), .out(OPND), .sel(ADDR10[9]));
  Multiplexer #(.select(2), .width(16), .enable("false")) multiplexer_3 (
    .in0(MEMDATA), .in1(IMMEXT), .in2(A_o), .in3(ALURES), .out(REGWDATA), .sel(CW[3:2]));
  Multiplexer #(.select(2), .width(16), .enable("false")) multiplexer_4 (
    .in0(IMMEXT), .in1(SP), .in2(SPDECV), .in3(IMMEXT), .out(MEMADDR), .sel(CW[6:5]));
  Multiplexer #(.select(1), .width(16), .enable("false")) multiplexer_5 (
    .in0(OPND), .in1(PCPLUS1), .out(MEMWDATA), .sel(isCall));
  Multiplexer #(.select(3), .enable("false")) multiplexer_6 (
    .in0(1'b0), .in1(FLAG[0]), .in2(FLAG[1]), .in3(FLAG[2]), .in4(FLAG[3]), .in5(1'b1), .in6(1'b1),
    .in7(1'b1), .out(PCLOAD[0]), .sel(CW[10:8]));
  Multiplexer #(.select(1), .width(16), .enable("false")) multiplexer_7 (
    .in0(ADDREXT), .in1(MEMDATA), .out(PCTARGET), .sel(isRet));
  Register #(.width(16)) A (.D(ALURES), .en(CW[0]), .Q(A_o), .clk(CLK), .clr(1'b0));
  Register #(.width(16)) X (.D(REGWDATA), .en(weX[0]), .Q(X_o), .clk(CLK), .clr(1'b0));
  Register #(.width(16)) Y (.D(REGWDATA), .en(weY[0]), .Q(Y_o), .clk(CLK), .clr(1'b0));
  Register #(.width(4)) u_FLAG (.D({1'b0, C_ADD, FLAGIN}), .en(CW[7]), .Q(FLAG), .clk(CLK), .clr(1'b0));
  Counter #(.width(16), .max('hffff)) u_SP (
    .load(1'b0), .count(spEn[0]), .Q(SP), .up(CW[12]), .clk(CLK), .clr(1'b0));  // open: D, carry
  Bit_Extender #(.in_width(16), .out_width(4), .\type ("zero")) bit_extender_4 (.in(OPND), .out(SHAMT));
  Subtractor #(.width(16)) subtractor_1 (.a(SP), .b(16'h1), .out(SPDECV), .bin(1'b0));  // open: bout
  Adder #(.width(16)) adder_2 (.a(A_o), .b(OPND), .out(R_ADD), .cin(1'b0), .cout(C_ADD));
  Subtractor #(.width(16)) subtractor_2 (.a(A_o), .b(OPND), .out(R_SUB), .bin(1'b0), .bout(B_SUB));
  assign R_AND = A_o & OPND;  // AND_Gate and_3, 16 bits wide
  assign R_OR = A_o | OPND;  // OR_Gate or_2, 16 bits wide
  // XOR_Gate xor_1 has open pins: out=R_XOR
  assign R_NOT = ~A_o;  // NOT_Gate not_2, 16 bits wide
  Shifter #(.shift("ll"), .width(16)) shifter_1 (.in(A_o), .\dist (SHAMT), .out(R_LSL));
  Shifter #(.shift("lr"), .width(16)) shifter_2 (.in(A_o), .\dist (SHAMT), .out(R_LSR));
  Shifter #(.shift("rl"), .width(16)) shifter_3 (.in(A_o), .\dist (SHAMT), .out(R_RSL));
  Shifter #(.shift("rr"), .width(16)) shifter_4 (.in(A_o), .\dist (SHAMT), .out(R_RSR));
  Multiplier #(.width(16)) multiplier_1 (.a(A_o), .b(OPND), .out(R_MUL), .cin({16{1'b0}}));  // open: cout
  Divider #(.width(16)) divider_1 (.a(A_o), .b(OPND), .out(R_DIV), .upper({16{1'b0}}), .rem(R_MOD));
  Adder #(.width(16)) adder_3 (.a(A_o), .b(16'h1), .out(R_INC), .cin(1'b0));  // open: cout
  Subtractor #(.width(16)) subtractor_3 (.a(A_o), .b(16'h1), .out(R_DEC), .bin(1'b0));  // open: bout
  Bit_Extender #(.in_width(16), .out_width(8), .\type ("zero")) bit_extender_5 (.in(MEMADDR), .out(bit_extender_5_out));
  RAM #(.addrWidth(8), .dataWidth(16), .asyncread("true")) DATA (
    .addr(bit_extender_5_out), .we(CW[4]), .oe(1'b1), .clk(CLK), .din(MEMWDATA), .dout(MEMDATA));
  Multiplexer #(.select(4), .width(16), .enable("false")) multiplexer_8 (
    .in0(R_ADD), .in1(R_SUB), .in2(R_AND), .in3(R_OR), .in4(R_XOR), .in5(R_NOT), .in6(R_LSL), .in7(R_LSR),
    .in8(R_RSL), .in9(R_RSR), .in10(R_MUL), .in11(R_DIV), .in12(R_MOD), .in13(R_INC), .in14(R_DEC),
    .in15(OPND), .out(ALURES), .sel(ALUOP));
  Comparator #(.width(16)) comparator_3 (.a(ALURES), .b({16{1'b0}}), .eq(FLAGIN[0]));  // open: gt, lt
  Comparator #(.width(16), .mode("twosComplement")) comparator_4 (
    .a(ALURES), .b({16{1'b0}}), .lt(FLAGIN[1]));  // open: gt, eq
  // Pins of 1 and 16 bits meet at PCLOAD
  // Pins of 1 and 16 bits meet at NREGBIT
  // Pins of 1 and 16 bits meet at weX
  // Pins of 1 and 16 bits meet at weY
  // Pins of 4 and 16 bits meet at {undriven, FLAG}
  // Pins of 1 and 16 bits meet at spEn

  // Other names for the same wires on the sheet: A[15:0] = A_o; writeA = CW[0]; writeReg = CW[1];
  //   regSrc[1:0] = CW[3:2]; memW = CW[4]; memAddr_t[1:0] = CW[6:5]; updFlags = CW[7]; pcSel[2:0] = CW[10:8];
  //   spDec = CW[11]; spInc = CW[12]; CW[18:13] = {aluOpSel, cAluOp, halt}; cwUnused = CW[19]; Zf = FLAG[0];
  //   Nf = FLAG[1]; Cf = FLAG[2]; Vf = FLAG[3]; fZ = FLAGIN[0]; fN = FLAGIN[1]; fC = C_ADD; FLAGIN[2] = C_ADD;
  //   IMM9[8:0] = ADDR10[8:0]; INSTR[9:0] = ADDR10; REGBIT = ADDR10[9]; OPCODE[5:0] = INSTR;
  //   OPLOW4[3:0] = INSTR[13:10]; X[15:0] = X_o; Y[15:0] = Y_o

  // Notes on the sheet:
  //   contents of PROG (hex, n*v repeats v):
  //   6805 6a03 3c00 200 fc00
  //   contents of CTRL (hex, n*v repeats v):
  //   81 81 81 81 81 81 81 81 81 81 81 81 81 81 81 81 44080 48080 0 0 0 0 0 0 2 10 6 850 1022 0 0 0 100
  //   200 300 400 500 e50 1720 0 0 0 0 0 0 0 0 0 0 0 0 0 0 0 0 0 0 0 0 0 0 0 0 2000
endmodule

module ALU (
  input  [15:0] A,
  input  [15:0] B,
  input  [3:0] OP,
  output [15:0] R,
  output Z,
  output N,
  output Cf,
  output V
);

  wire B_SUB, DIFFAR, EQAB, SA, SAxSB, SB, SR;
  wire [3:0] SHAMT;
  wire [15:0] R_ADD, R_AND, R_DEC, R_DIV, R_INC, R_LSL, R_LSR, R_MOD, R_MUL, R_NOT, R_OR, R_RSL, R_RSR,
       R_SUB, R_XOR;

  Bit_Extender #(.in_width(16), .out_width(4), .\type ("zero")) bit_extender_1 (.in(B), .out(SHAMT));
  Adder #(.width(16)) adder_1 (.a(A), .b(B), .out(R_ADD), .cin(1'b0), .cout(Cf));
  Subtractor #(.width(16)) subtractor_1 (.a(A), .b(B), .out(R_SUB), .bin(1'b0), .bout(B_SUB));
  assign R_AND = A & B;  // AND_Gate and_1, 16 bits wide
  assign R_OR = A | B;  // OR_Gate or_1, 16 bits wide
  // XOR_Gate xor_1 has open pins: out=R_XOR
  assign R_NOT = ~A;  // NOT_Gate not_1, 16 bits wide
  Shifter #(.shift("ll"), .width(16)) shifter_1 (.in(A), .\dist (SHAMT), .out(R_LSL));
  Shifter #(.shift("lr"), .width(16)) shifter_2 (.in(A), .\dist (SHAMT), .out(R_LSR));
  Shifter #(.shift("rl"), .width(16)) shifter_3 (.in(A), .\dist (SHAMT), .out(R_RSL));
  Shifter #(.shift("rr"), .width(16)) shifter_4 (.in(A), .\dist (SHAMT), .out(R_RSR));
  Multiplier #(.width(16)) multiplier_1 (.a(A), .b(B), .out(R_MUL), .cin({16{1'b0}}));  // open: cout
  Divider #(.width(16)) divider_1 (.a(A), .b(B), .out(R_DIV), .upper({16{1'b0}}), .rem(R_MOD));
  Adder #(.width(16)) adder_2 (.a(A), .b(16'h1), .out(R_INC), .cin(1'b0));  // open: cout
  Subtractor #(.width(16)) subtractor_2 (.a(A), .b(16'h1), .out(R_DEC), .bin(1'b0));  // open: bout
  Multiplexer #(.select(4), .width(16), .enable("false")) multiplexer_1 (
    .in0(R_ADD), .in1(R_SUB), .in2(R_AND), .in3(R_OR), .in4(R_XOR), .in5(R_NOT), .in6(R_LSL), .in7(R_LSR),
    .in8(R_RSL), .in9(R_RSR), .in10(R_MUL), .in11(R_DIV), .in12(R_MOD), .in13(R_INC), .in14(R_DEC), .in15(B),
    .out(R), .sel(OP));
  Comparator #(.width(16)) comparator_1 (.a(R), .b({16{1'b0}}), .eq(Z));  // open: gt, lt
  Comparator #(.width(16), .mode("twosComplement")) comparator_2 (.a(R), .b({16{1'b0}}), .lt(N));  // open: gt, eq
  Comparator #(.width(16), .mode("twosComplement")) comparator_3 (.a(A), .b({16{1'b0}}), .lt(SA));  // open: gt, eq
  Comparator #(.width(16), .mode("twosComplement")) comparator_4 (.a(B), .b({16{1'b0}}), .lt(SB));  // open: gt, eq
  Comparator #(.width(16), .mode("twosComplement")) comparator_5 (.a(R_ADD), .b({16{1'b0}}), .lt(SR));  // open: gt, eq
  // XOR_Gate xor_2 has open pins: out=SAxSB
  // XOR_Gate xor_3 has open pins: out=DIFFAR
  not not_2 (EQAB, SAxSB);
  and and_2 (V, EQAB, DIFFAR);

  // Other names for the same wires on the sheet: C_ADD = Cf
endmodule
